# Fritzing sketch arduinoPr (saved by Fritzing 0.9.3b)
circuit board: 8.46667cm x 5.64444cm
breadboards: 1

parts:
  LCD1 = LCD screen
  R1 = Resistor [tolerance=±5% resistance=220 package=THT]
  Part1 = Arduino Uno (Rev3)
  LED1 = LED - 5mm [color="Red (633nm)" package="5 mm [THT]"]
  R2 = Resistor [tolerance=±5% resistance=220 package=THT]
  U1 = ESP8266 WiFi Module [part_number=ESP8266]
  M1 = E18-D80NK_1 [package=THT]
  M2 = E18-D80NK_1 [package=THT]

nets:
  GND: LCD1.VSS, LCD1.R/W, LCD1.LED-, R1.Pin_1, Part1.GND, U1.GND, M1.pin1, M2.pin1
  VDD: LCD1.VDD, LCD1.LED+, Part1.5V, M1.pin2, M2.pin2
  N1: LCD1.V0, R1.Pin_0
  N2: LCD1.RS, Part1.D11_PWM/MOSI
  N3: LCD1.E, Part1.D12/MISO
  N4: LCD1.DB4, Part1.D7
  N5: LCD1.DB5, Part1.D6_PWM
  N6: LCD1.DB6, Part1.D5_PWM
  N7: LCD1.DB7, Part1.D4
  N8: Part1.A0, M1.pin3
  N9: Part1.A5/SCL, M2.pin3
  N10: Part1.D0/RX, U1.TXD
  N11: Part1.D1/TX, U1.RXD
  3V3: Part1.3V3, U1.VCC, U1.CH_PD
  N12: LED1.anode, R2.Pin_0

custom parts:
  ESP8266 WiFi Module: Generic WiFi Module based on the ESP8266 with onboard PCB antenna and UART communications
  E18-D80NK_1: E18-D80NK Proximity Sensor module.
